// Logisim project CPU.circ as structural Verilog: 1 circuit, main circuit CPU
module CPU (
);

  wire and_1_out, and_2_out, clock_1_out, decoder_1_out0, decoder_1_out1, decoder_1_out2, decoder_1_out3,
       decoder_1_out4, decoder_1_out5, or_1_out;
  wire [3:0] rom_1_data, rom_1_data_2, rom_1_data_4, rom_1_data_5;
  wire [6:0] bit_extender_2_out;
  wire [15:0] main_1_p1, main_1_p6, main_1_p7, ram_1_data;
  wire [23:0] adder_1_out, bit_extender_1_out, multiplexer_1_out, register_1_q, rom_1_data_3;
  wire [31:0] register_2_q, register_3_q;

  Multiplexer #(.width(24), .enable("false")) multiplexer_1 (
    .in0({rom_1_data_3[23:16], rom_1_data_5, rom_1_data_3[11:8], rom_1_data_4, rom_1_data_3[3:0]}),
    .in1(adder_1_out), .out(multiplexer_1_out), .sel(decoder_1_out3));
  assign bit_extender_1_out = {{23{1'b0}}, 1'b1};  // Bit_Extender bit_extender_1
  Register #(.width(24)) register_1 (.D(multiplexer_1_out), .Q(register_1_q), .clk(clock_1_out));  // open: en, clr
  Adder #(.width(24)) adder_1 (.a(register_1_q), .b(bit_extender_1_out), .out(adder_1_out));  // open: cin, cout
  ROM #(.addrWidth(24), .dataWidth(32)) rom_1 (
    .addr(register_1_q),
    .data({rom_1_data_5, rom_1_data_3[11:8], rom_1_data_4, rom_1_data_3[3:0], rom_1_data_3[23:16], rom_1_data_2, rom_1_data}));  // open: sel
  Decoder #(.select(4), .enable("false")) decoder_1 (
    .out0(decoder_1_out0), .out1(decoder_1_out1), .out2(decoder_1_out2), .out3(decoder_1_out3),
    .out4(decoder_1_out4), .out5(decoder_1_out5), .sel(rom_1_data));  // open: out6, out7, out8, out9, out10, out11, out12, out13, out14, out15
  or or_1 (or_1_out, decoder_1_out1, decoder_1_out2, decoder_1_out0);
  Clock clock_1 (.out(clock_1_out));
  ALU alu_1 (.A(main_1_p7), .B(main_1_p1), .Enable(decoder_1_out2));  // open: INSTR, OUT
  and and_1 (and_1_out, decoder_1_out1, rom_1_data_2[0]);
  and and_2 (and_2_out, rom_1_data_2[1], decoder_1_out1);
  // REGARRAY_main main_1: pin names not known; wires that end beside it: main_1_p1, main_1_p1[15:12], rom_1_data_3[23:20], or_1_out, clock_1_out, main_1_p6, main_1_p7
  Multiplexer #(.select(2), .width(16)) multiplexer_2 (
    .in1(ram_1_data), .in2(main_1_p6),
    .in3({rom_1_data_5, rom_1_data_3[11:8], rom_1_data_4, rom_1_data_3[3:0]}), .out(main_1_p1));  // open: in0, sel, en
  Register #(.width(32)) register_2 (.Q(register_2_q), .clk(clock_1_out));  // open: D, en, clr
  Register #(.width(32)) register_3 (.Q(register_3_q), .clk(clock_1_out));  // open: D, en, clr
  RAM #(.dataWidth(16), .bus("separate")) ram_1 (
    .addr(rom_1_data_3[23:16]), .din(main_1_p1), .data(ram_1_data), .sel(and_1_out), .clk(clock_1_out),
    .ld(and_2_out));  // open: str, clr
  Bit_Extender #(.out_width(7)) bit_extender_2 (.in(main_1_p1[15:8]), .out(bit_extender_2_out));
  DotMatrix #(.matrixcols(8), .matrixrows(8)) dotmatrix_1 (
    .col0(register_2_q[31:24]), .col1(register_2_q[23:16]), .col2(register_2_q[15:8]),
    .col3(register_2_q[7:0]), .col4(register_3_q[31:24]), .col5(register_3_q[23:16]),
    .col6(register_3_q[15:8]), .col7(register_3_q[7:0]));
  TTY #(.rows(32), .cols(100)) tty_1 (
    .data(bit_extender_2_out), .clk(clock_1_out), .we(decoder_1_out4), .clr(decoder_1_out5));

  // Notes on the sheet:
  //   0=immediate
  //   1=mov
  //   2=calc
  //   3=jmp
  //   4=wrt
  //   5=rssc
  //   contents of rom_1 (hex, n*v repeats v):
  //   65536 4108
  //   Write
  //   Read
endmodule
